// Digital circuit llbc_keystep.dig as structural Verilog
module llbc_keystep (
  input  [63:0] k0,
  input  [63:0] k1,
  input  [63:0] rc,
  output [63:0] k0_2,
  output [63:0] k1_2
);

  wire [15:0] n11, n12, n24, n25;

  assign n11 = {k1[60:48], k1[63:61]} ^ k1[31:16];  // XOr xor_1, 16 bits wide
  assign n12 = {k1[46:32], k1[47]} ^ k1[15:0];  // XOr xor_2, 16 bits wide
  assign n24 = {n11[12:0], n11[15:13]} ^ {k1[60:48], k1[63:61]};  // XOr xor_3, 16 bits wide
  assign n25 = {n12[14:0], n12[15]} ^ {k1[46:32], k1[47]};  // XOr xor_4, 16 bits wide
  assign k1_2 = {n24, n25, n11[12:0], n11[15:13], n12[14:0], n12[15]} ^ k0 ^ rc;  // XOr xor_5, 64 bits wide

  assign k0_2 = k1;

  // Other names for the same wires on the sheet: n0[63:0] = k1; n10[15:0] = k1[15:0]; n8[15:0] = k1[31:16];
  //   n4[15:0] = k1[47:32]; n5[14:0] = k1[46:32]; n9[15:0] = {k1[46:32], k1[47]};
  //   n13[63:0] = {n11, n12, k1[60:48], k1[63:61], k1[46:32], k1[47]}; n23[15:0] = {k1[46:32], k1[47]}; n6 = k1[47];
  //   n1[15:0] = k1[63:48]; n2[12:0] = k1[60:48]; n7[15:0] = {k1[60:48], k1[63:61]};
  //   n21[15:0] = {k1[60:48], k1[63:61]}; n3[2:0] = k1[63:61]; n14[15:0] = n11; n15[12:0] = n11[12:0];
  //   n20[15:0] = {n11[12:0], n11[15:13]}; n26[63:0] = {n24, n25, n11[12:0], n11[15:13], n12[14:0], n12[15]};
  //   n16[2:0] = n11[15:13]; n17[15:0] = n12; n18[14:0] = n12[14:0]; n22[15:0] = {n12[14:0], n12[15]}; n19 = n12[15];
  //   n27[63:0] = k0; n28[63:0] = rc; n29[63:0] = k1_2
endmodule
