// Digital circuit llbc_round.dig as structural Verilog
module llbc_round (
  input  [63:0] L,
  input  [63:0] R,
  input  [63:0] rk_lo,
  input  [63:0] rk_hi,
  output [63:0] Lnext,
  output [63:0] Rnext
);

  wire [3:0] n8, n10, n12, n14, n16, n18, n20, n22, n24, n26, n28, n30, n32, n34, n36, n38, n44, n46, n48,
       n50, n52, n54, n56, n58, n60, n62, n64, n66, n68, n70, n72, n74;
  wire [63:0] n77, n81, n85, n89, n93, n95;

  assign Rnext = L ^ rk_hi ^ 64'h243f6a8800000000;  // XOr xor_1, 64 bits wide
  ROM #(.Bits(4), .AddrBits(4)) A0 (.A({L[0], L[63:61]}), .sel(1'b1), .D(n8));
  ROM #(.Bits(4), .AddrBits(4)) A1 (.A(L[4:1]), .sel(1'b1), .D(n10));
  ROM #(.Bits(4), .AddrBits(4)) A2 (.A(L[8:5]), .sel(1'b1), .D(n12));
  ROM #(.Bits(4), .AddrBits(4)) A3 (.A(L[12:9]), .sel(1'b1), .D(n14));
  ROM #(.Bits(4), .AddrBits(4)) A4 (.A(L[16:13]), .sel(1'b1), .D(n16));
  ROM #(.Bits(4), .AddrBits(4)) A5 (.A(L[20:17]), .sel(1'b1), .D(n18));
  ROM #(.Bits(4), .AddrBits(4)) A6 (.A(L[24:21]), .sel(1'b1), .D(n20));
  ROM #(.Bits(4), .AddrBits(4)) A7 (.A(L[28:25]), .sel(1'b1), .D(n22));
  ROM #(.Bits(4), .AddrBits(4)) A8 (.A(L[32:29]), .sel(1'b1), .D(n24));
  ROM #(.Bits(4), .AddrBits(4)) A9 (.A(L[36:33]), .sel(1'b1), .D(n26));
  ROM #(.Bits(4), .AddrBits(4)) A10 (.A(L[40:37]), .sel(1'b1), .D(n28));
  ROM #(.Bits(4), .AddrBits(4)) A11 (.A(L[44:41]), .sel(1'b1), .D(n30));
  ROM #(.Bits(4), .AddrBits(4)) A12 (.A(L[48:45]), .sel(1'b1), .D(n32));
  ROM #(.Bits(4), .AddrBits(4)) A13 (.A(L[52:49]), .sel(1'b1), .D(n34));
  ROM #(.Bits(4), .AddrBits(4)) A14 (.A(L[56:53]), .sel(1'b1), .D(n36));
  ROM #(.Bits(4), .AddrBits(4)) A15 (.A(L[60:57]), .sel(1'b1), .D(n38));
  ROM #(.Bits(4), .AddrBits(4)) B0 (.A(Rnext[48:45]), .sel(1'b1), .D(n44));
  ROM #(.Bits(4), .AddrBits(4)) B1 (.A(Rnext[52:49]), .sel(1'b1), .D(n46));
  ROM #(.Bits(4), .AddrBits(4)) B2 (.A(Rnext[56:53]), .sel(1'b1), .D(n48));
  ROM #(.Bits(4), .AddrBits(4)) B3 (.A(Rnext[60:57]), .sel(1'b1), .D(n50));
  ROM #(.Bits(4), .AddrBits(4)) B4 (.A({Rnext[0], Rnext[63:61]}), .sel(1'b1), .D(n52));
  ROM #(.Bits(4), .AddrBits(4)) B5 (.A(Rnext[4:1]), .sel(1'b1), .D(n54));
  ROM #(.Bits(4), .AddrBits(4)) B6 (.A(Rnext[8:5]), .sel(1'b1), .D(n56));
  ROM #(.Bits(4), .AddrBits(4)) B7 (.A(Rnext[12:9]), .sel(1'b1), .D(n58));
  ROM #(.Bits(4), .AddrBits(4)) B8 (.A(Rnext[16:13]), .sel(1'b1), .D(n60));
  ROM #(.Bits(4), .AddrBits(4)) B9 (.A(Rnext[20:17]), .sel(1'b1), .D(n62));
  ROM #(.Bits(4), .AddrBits(4)) B10 (.A(Rnext[24:21]), .sel(1'b1), .D(n64));
  ROM #(.Bits(4), .AddrBits(4)) B11 (.A(Rnext[28:25]), .sel(1'b1), .D(n66));
  ROM #(.Bits(4), .AddrBits(4)) B12 (.A(Rnext[32:29]), .sel(1'b1), .D(n68));
  ROM #(.Bits(4), .AddrBits(4)) B13 (.A(Rnext[36:33]), .sel(1'b1), .D(n70));
  ROM #(.Bits(4), .AddrBits(4)) B14 (.A(Rnext[40:37]), .sel(1'b1), .D(n72));
  ROM #(.Bits(4), .AddrBits(4)) B15 (.A(Rnext[44:41]), .sel(1'b1), .D(n74));
  assign n77 = {n74, n72, n70, n68, n66, n64, n62, n60, n58, n56, n54, n52, n50, n48, n46, n44} ^ {n38, n36, n34, n32, n30, n28, n26, n24, n22, n20, n18, n16, n14, n12, n10, n8};  // XOr xor_2, 64 bits wide
  assign n81 = {n77[60:0], n77[63:61]} ^ {n74, n72, n70, n68, n66, n64, n62, n60, n58, n56, n54, n52, n50, n48, n46, n44};  // XOr xor_3, 64 bits wide
  assign n85 = {n81[44:0], n81[63:45]} ^ n77;  // XOr xor_4, 64 bits wide
  assign n89 = {n85[60:0], n85[63:61]} ^ n81;  // XOr xor_5, 64 bits wide
  assign n93 = {n89[44:0], n89[63:45]} ^ n85;  // XOr xor_6, 64 bits wide
  assign n95 = n89 ^ n93;  // XOr xor_7, 64 bits wide
  assign Lnext = R ^ n95 ^ rk_lo;  // XOr xor_8, 64 bits wide

  // Other names for the same wires on the sheet: n0[63:0] = L; n3[60:0] = L[60:0]; n5[63:0] = {L[60:0], L[63:61]};
  //   n6[3:0] = {L[0], L[63:61]}; n9[3:0] = L[4:1]; n11[3:0] = L[8:5]; n13[3:0] = L[12:9]; n15[3:0] = L[16:13];
  //   n17[3:0] = L[20:17]; n19[3:0] = L[24:21]; n21[3:0] = L[28:25]; n23[3:0] = L[32:29]; n25[3:0] = L[36:33];
  //   n27[3:0] = L[40:37]; n29[3:0] = L[44:41]; n31[3:0] = L[48:45]; n33[3:0] = L[52:49]; n35[3:0] = L[56:53];
  //   n37[3:0] = L[60:57]; n4[2:0] = L[63:61]; n1[63:0] = rk_hi;
  //   n76[63:0] = {n38, n36, n34, n32, n30, n28, n26, n24, n22, n20, n18, n16, n14, n12, n10, n8}; n39[63:0] = Rnext;
  //   n40[44:0] = Rnext[44:0]; n42[63:0] = {Rnext[44:0], Rnext[63:45]}; n51[3:0] = {Rnext[0], Rnext[63:61]};
  //   n53[3:0] = Rnext[4:1]; n55[3:0] = Rnext[8:5]; n57[3:0] = Rnext[12:9]; n59[3:0] = Rnext[16:13];
  //   n61[3:0] = Rnext[20:17]; n63[3:0] = Rnext[24:21]; n65[3:0] = Rnext[28:25]; n67[3:0] = Rnext[32:29];
  //   n69[3:0] = Rnext[36:33]; n71[3:0] = Rnext[40:37]; n73[3:0] = Rnext[44:41]; n41[18:0] = Rnext[63:45];
  //   n43[3:0] = Rnext[48:45]; n45[3:0] = Rnext[52:49]; n47[3:0] = Rnext[56:53]; n49[3:0] = Rnext[60:57];
  //   n75[63:0] = {n74, n72, n70, n68, n66, n64, n62, n60, n58, n56, n54, n52, n50, n48, n46, n44};
  //   n78[60:0] = n77[60:0]; n80[63:0] = {n77[60:0], n77[63:61]}; n79[2:0] = n77[63:61]; n82[44:0] = n81[44:0];
  //   n84[63:0] = {n81[44:0], n81[63:45]}; n83[18:0] = n81[63:45]; n86[60:0] = n85[60:0];
  //   n88[63:0] = {n85[60:0], n85[63:61]}; n87[2:0] = n85[63:61]; n90[44:0] = n89[44:0];
  //   n92[63:0] = {n89[44:0], n89[63:45]}; n91[18:0] = n89[63:45]; n94[63:0] = R; n96[63:0] = rk_lo;
  //   n97[63:0] = Lnext

  // Notes on the sheet:
  //   contents of A0 (hex, n*v repeats v):
  //   4,7,5,1,c,b,d,8,e,f,6,3,a,9,2,0
  //   contents of A1 (hex, n*v repeats v):
  //   4,7,5,1,c,b,d,8,e,f,6,3,a,9,2,0
  //   contents of A2 (hex, n*v repeats v):
  //   4,7,5,1,c,b,d,8,e,f,6,3,a,9,2,0
  //   contents of A3 (hex, n*v repeats v):
  //   4,7,5,1,c,b,d,8,e,f,6,3,a,9,2,0
  //   contents of A4 (hex, n*v repeats v):
  //   4,7,5,1,c,b,d,8,e,f,6,3,a,9,2,0
  //   contents of A5 (hex, n*v repeats v):
  //   4,7,5,1,c,b,d,8,e,f,6,3,a,9,2,0
  //   contents of A6 (hex, n*v repeats v):
  //   4,7,5,1,c,b,d,8,e,f,6,3,a,9,2,0
  //   contents of A7 (hex, n*v repeats v):
  //   4,7,5,1,c,b,d,8,e,f,6,3,a,9,2,0
  //   contents of A8 (hex, n*v repeats v):
  //   4,7,5,1,c,b,d,8,e,f,6,3,a,9,2,0
  //   contents of A9 (hex, n*v repeats v):
  //   4,7,5,1,c,b,d,8,e,f,6,3,a,9,2,0
  //   contents of A10 (hex, n*v repeats v):
  //   4,7,5,1,c,b,d,8,e,f,6,3,a,9,2,0
  //   contents of A11 (hex, n*v repeats v):
  //   4,7,5,1,c,b,d,8,e,f,6,3,a,9,2,0
  //   contents of A12 (hex, n*v repeats v):
  //   4,7,5,1,c,b,d,8,e,f,6,3,a,9,2,0
  //   contents of A13 (hex, n*v repeats v):
  //   4,7,5,1,c,b,d,8,e,f,6,3,a,9,2,0
  //   contents of A14 (hex, n*v repeats v):
  //   4,7,5,1,c,b,d,8,e,f,6,3,a,9,2,0
  //   contents of A15 (hex, n*v repeats v):
  //   4,7,5,1,c,b,d,8,e,f,6,3,a,9,2,0
  //   contents of B0 (hex, n*v repeats v):
  //   e,c,8,4,b,d,1,5,f,3,a,2,9,7,0,6
  //   contents of B1 (hex, n*v repeats v):
  //   e,c,8,4,b,d,1,5,f,3,a,2,9,7,0,6
  //   contents of B2 (hex, n*v repeats v):
  //   e,c,8,4,b,d,1,5,f,3,a,2,9,7,0,6
  //   contents of B3 (hex, n*v repeats v):
  //   e,c,8,4,b,d,1,5,f,3,a,2,9,7,0,6
  //   contents of B4 (hex, n*v repeats v):
  //   e,c,8,4,b,d,1,5,f,3,a,2,9,7,0,6
  //   contents of B5 (hex, n*v repeats v):
  //   e,c,8,4,b,d,1,5,f,3,a,2,9,7,0,6
  //   contents of B6 (hex, n*v repeats v):
  //   e,c,8,4,b,d,1,5,f,3,a,2,9,7,0,6
  //   contents of B7 (hex, n*v repeats v):
  //   e,c,8,4,b,d,1,5,f,3,a,2,9,7,0,6
  //   contents of B8 (hex, n*v repeats v):
  //   e,c,8,4,b,d,1,5,f,3,a,2,9,7,0,6
  //   contents of B9 (hex, n*v repeats v):
  //   e,c,8,4,b,d,1,5,f,3,a,2,9,7,0,6
  //   contents of B10 (hex, n*v repeats v):
  //   e,c,8,4,b,d,1,5,f,3,a,2,9,7,0,6
  //   contents of B11 (hex, n*v repeats v):
  //   e,c,8,4,b,d,1,5,f,3,a,2,9,7,0,6
  //   contents of B12 (hex, n*v repeats v):
  //   e,c,8,4,b,d,1,5,f,3,a,2,9,7,0,6
  //   contents of B13 (hex, n*v repeats v):
  //   e,c,8,4,b,d,1,5,f,3,a,2,9,7,0,6
  //   contents of B14 (hex, n*v repeats v):
  //   e,c,8,4,b,d,1,5,f,3,a,2,9,7,0,6
  //   contents of B15 (hex, n*v repeats v):
  //   e,c,8,4,b,d,1,5,f,3,a,2,9,7,0,6
endmodule
