// Digital circuit subcell.dig as structural Verilog
module subcell (
  input  [63:0] x,
  output [63:0] y
);

  ROM #(.Bits(4), .AddrBits(4)) S0 (.A(x[3:0]), .sel(1'b1), .D(y[3:0]));
  ROM #(.Bits(4), .AddrBits(4)) S1 (.A(x[7:4]), .sel(1'b1), .D(y[7:4]));
  ROM #(.Bits(4), .AddrBits(4)) S2 (.A(x[11:8]), .sel(1'b1), .D(y[11:8]));
  ROM #(.Bits(4), .AddrBits(4)) S3 (.A(x[15:12]), .sel(1'b1), .D(y[15:12]));
  ROM #(.Bits(4), .AddrBits(4)) S4 (.A(x[19:16]), .sel(1'b1), .D(y[19:16]));
  ROM #(.Bits(4), .AddrBits(4)) S5 (.A(x[23:20]), .sel(1'b1), .D(y[23:20]));
  ROM #(.Bits(4), .AddrBits(4)) S6 (.A(x[27:24]), .sel(1'b1), .D(y[27:24]));
  ROM #(.Bits(4), .AddrBits(4)) S7 (.A(x[31:28]), .sel(1'b1), .D(y[31:28]));
  ROM #(.Bits(4), .AddrBits(4)) S8 (.A(x[35:32]), .sel(1'b1), .D(y[35:32]));
  ROM #(.Bits(4), .AddrBits(4)) S9 (.A(x[39:36]), .sel(1'b1), .D(y[39:36]));
  ROM #(.Bits(4), .AddrBits(4)) S10 (.A(x[43:40]), .sel(1'b1), .D(y[43:40]));
  ROM #(.Bits(4), .AddrBits(4)) S11 (.A(x[47:44]), .sel(1'b1), .D(y[47:44]));
  ROM #(.Bits(4), .AddrBits(4)) S12 (.A(x[51:48]), .sel(1'b1), .D(y[51:48]));
  ROM #(.Bits(4), .AddrBits(4)) S13 (.A(x[55:52]), .sel(1'b1), .D(y[55:52]));
  ROM #(.Bits(4), .AddrBits(4)) S14 (.A(x[59:56]), .sel(1'b1), .D(y[59:56]));
  ROM #(.Bits(4), .AddrBits(4)) S15 (.A(x[63:60]), .sel(1'b1), .D(y[63:60]));

  // Other names for the same wires on the sheet: n0[63:0] = x; n1[3:0] = x[3:0]; n4[3:0] = x[7:4]; n6[3:0] = x[11:8];
  //   n8[3:0] = x[15:12]; n10[3:0] = x[19:16]; n12[3:0] = x[23:20]; n14[3:0] = x[27:24]; n16[3:0] = x[31:28];
  //   n18[3:0] = x[35:32]; n20[3:0] = x[39:36]; n22[3:0] = x[43:40]; n24[3:0] = x[47:44]; n26[3:0] = x[51:48];
  //   n28[3:0] = x[55:52]; n30[3:0] = x[59:56]; n32[3:0] = x[63:60]; n3[3:0] = y[3:0]; n34[63:0] = y;
  //   n5[3:0] = y[7:4]; n7[3:0] = y[11:8]; n9[3:0] = y[15:12]; n11[3:0] = y[19:16]; n13[3:0] = y[23:20];
  //   n15[3:0] = y[27:24]; n17[3:0] = y[31:28]; n19[3:0] = y[35:32]; n21[3:0] = y[39:36]; n23[3:0] = y[43:40];
  //   n25[3:0] = y[47:44]; n27[3:0] = y[51:48]; n29[3:0] = y[55:52]; n31[3:0] = y[59:56]; n33[3:0] = y[63:60]

  // Notes on the sheet:
  //   contents of S0 (hex, n*v repeats v):
  //   4,7,5,1,c,b,d,8,e,f,6,3,a,9,2,0
  //   contents of S1 (hex, n*v repeats v):
  //   4,7,5,1,c,b,d,8,e,f,6,3,a,9,2,0
  //   contents of S2 (hex, n*v repeats v):
  //   4,7,5,1,c,b,d,8,e,f,6,3,a,9,2,0
  //   contents of S3 (hex, n*v repeats v):
  //   4,7,5,1,c,b,d,8,e,f,6,3,a,9,2,0
  //   contents of S4 (hex, n*v repeats v):
  //   4,7,5,1,c,b,d,8,e,f,6,3,a,9,2,0
  //   contents of S5 (hex, n*v repeats v):
  //   4,7,5,1,c,b,d,8,e,f,6,3,a,9,2,0
  //   contents of S6 (hex, n*v repeats v):
  //   4,7,5,1,c,b,d,8,e,f,6,3,a,9,2,0
  //   contents of S7 (hex, n*v repeats v):
  //   4,7,5,1,c,b,d,8,e,f,6,3,a,9,2,0
  //   contents of S8 (hex, n*v repeats v):
  //   4,7,5,1,c,b,d,8,e,f,6,3,a,9,2,0
  //   contents of S9 (hex, n*v repeats v):
  //   4,7,5,1,c,b,d,8,e,f,6,3,a,9,2,0
  //   contents of S10 (hex, n*v repeats v):
  //   4,7,5,1,c,b,d,8,e,f,6,3,a,9,2,0
  //   contents of S11 (hex, n*v repeats v):
  //   4,7,5,1,c,b,d,8,e,f,6,3,a,9,2,0
  //   contents of S12 (hex, n*v repeats v):
  //   4,7,5,1,c,b,d,8,e,f,6,3,a,9,2,0
  //   contents of S13 (hex, n*v repeats v):
  //   4,7,5,1,c,b,d,8,e,f,6,3,a,9,2,0
  //   contents of S14 (hex, n*v repeats v):
  //   4,7,5,1,c,b,d,8,e,f,6,3,a,9,2,0
  //   contents of S15 (hex, n*v repeats v):
  //   4,7,5,1,c,b,d,8,e,f,6,3,a,9,2,0
endmodule
