// Digital circuit gen_sbox.dig as structural Verilog
module gen_sbox (
  input  [3:0] x,
  output [3:0] y
);

  ROM #(.Bits(4), .AddrBits(4)) S (.A(x), .sel(1'b1), .D(y));

  // Notes on the sheet:
  //   contents of S (hex, n*v repeats v):
  //   c,5,6,b,9,0,a,d,3,e,f,8,4,7,1,2
endmodule

/* Test case t:
x y
0x0 0xC
0x1 0x5
0x2 0x6
0x3 0xB
0x4 0x9
0x5 0x0
0x6 0xA
0x7 0xD
0x8 0x3
0x9 0xE
0xA 0xF
0xB 0x8
0xC 0x4
0xD 0x7
0xE 0x1
0xF 0x2
*/
