// Digital circuit mixword.dig as structural Verilog
module mixword (
  input  [63:0] s1o,
  input  [63:0] s2o,
  output [63:0] m
);

  wire [63:0] n2, n6, n10, n14, n18;

  assign n2 = s2o ^ s1o;  // XOr xor_1, 64 bits wide
  assign n6 = {n2[60:0], n2[63:61]} ^ s2o;  // XOr xor_2, 64 bits wide
  assign n10 = {n6[44:0], n6[63:45]} ^ n2;  // XOr xor_3, 64 bits wide
  assign n14 = {n10[60:0], n10[63:61]} ^ n6;  // XOr xor_4, 64 bits wide
  assign n18 = {n14[44:0], n14[63:45]} ^ n10;  // XOr xor_5, 64 bits wide
  assign m = n14 ^ n18;  // XOr xor_6, 64 bits wide

  // Other names for the same wires on the sheet: n0[63:0] = s2o; n1[63:0] = s1o; n3[60:0] = n2[60:0];
  //   n5[63:0] = {n2[60:0], n2[63:61]}; n4[2:0] = n2[63:61]; n7[44:0] = n6[44:0]; n9[63:0] = {n6[44:0], n6[63:45]};
  //   n8[18:0] = n6[63:45]; n11[60:0] = n10[60:0]; n13[63:0] = {n10[60:0], n10[63:61]}; n12[2:0] = n10[63:61];
  //   n15[44:0] = n14[44:0]; n17[63:0] = {n14[44:0], n14[63:45]}; n16[18:0] = n14[63:45]; n19[63:0] = m
endmodule
