// Digital circuit rol3.dig as structural Verilog
module rol3 (
  input  [63:0] x,
  output [63:0] y
);


  assign y = {x[60:0], x[63:61]};

  // Other names for the same wires on the sheet: n0[63:0] = x; n1[60:0] = x[60:0]; n3[63:0] = {x[60:0], x[63:61]};
  //   n2[2:0] = x[63:61]
endmodule
